# Fritzing sketch scheme (saved by Fritzing 0.9.10b)
breadboards: 1

parts:
  LED1 = smd LED [color="Red (633nm)" package="1206 [SMD]"]
  R1 = Resistor [tolerance=±5% resistance=220 package="2010 [SMD]"]
  Part1 = Soil Moisture Sensor
  R2 = Rotary Potentiometer (Small) [package=THT]
  R3 = Resistor [tolerance=±5% resistance=220 package="2010 [SMD]"]
  LED2 = smd LED [color="Red (633nm)" package="1206 [SMD]"]

nets:
  GND: LED1.cathode, Part1.GND, R2.GND, LED2.cathode
  N1: LED1.anode, R1.Pin_0
  VCC: Part1.VCC, R2.Vcc
  N2: R2.SIG, R3.Pin_1
  N3: R3.Pin_0, LED2.anode

notes:
  ARD_D8
  ARD_A1
  ARD_D7
  GND
  Vcc

custom parts:
  Rotary Potentiometer (Small): A rotary adjustable resistor (potentiometer).
